// Digital circuit hardware.dig as structural Verilog
module hardware (
  input  clk,
  input  in_2,
  input  in_3,
  input  in_4,
  input  [15:0] in_5,
  input  in_6
);

  wire and_2_out, Clk_t, control_1_alud, control_1_halt, control_1_hid, control_1_jmp, control_1_lod, Halt,
       InstrEx, InstrL, jumpdecider_1_jmp, PC_ovf, rs_ff_1_nq, rs_ff_1_q, RTW, Un_Halt_out;
  wire [3:0] alu_1_fl, control_1_aluop, control_1_jt, Flags_q, RA, RT;
  wire [7:0] control_1_imm, registerfile_1_da, registerfile_1_da_2;
  wire [15:0] add_1_s, alu_1_rdata, bitextender_1_out, driver_1_out, InstrReg_q, PC_out, ramdualport_1_d,
       registerfile_1_db;

  Button Un_Halt (.out(Un_Halt_out));
  CounterPreset #(.Bits(16)) PC (
    .en(InstrL), .C(Clk_t), .dir(in_2), .in(driver_1_out), .ld(and_2_out), .clr(in_3), .out(PC_out),
    .ovf(PC_ovf));
  RS_FF rs_ff_1 (.S(Halt), .C(clk), .R(Un_Halt_out), .Q(rs_ff_1_q), .nQ(rs_ff_1_nq));
  Counter Phase (.en(1'b1), .C(Clk_t), .clr(1'b0), .out(InstrEx));  // open: ovf
  // Probe on PC_ovf
  and and_1 (Clk_t, rs_ff_1_nq, clk);
  not not_1 (InstrL, InstrEx);
  LED Halted (.in(rs_ff_1_q));
  LED Running (.in(Clk_t));
  RAMDualPort #(.AddrBits(16), .isProgramMemory("true"), .Bits(16)) ramdualport_1 (
    .A(PC_out), .Din(in_5), .str(in_4), .C(Clk_t), .ld(1'b1), .D(ramdualport_1_d));
  Register #(.Bits(16)) InstrReg (.D(ramdualport_1_d), .C(Clk_t), .en(InstrL), .Q(InstrReg_q));
  RegisterFile #(.AddrBits(4), .Bits(16)) registerfile_1 (
    .Din(driver_1_out), .we(RTW), .Rw(RT), .C(Clk_t), .Ra(RT), .Rb(RA),
    .Da({registerfile_1_da_2, registerfile_1_da}), .Db(registerfile_1_db));
  // Probe on InstrReg_q
  control control_1 (
    .Instr(InstrReg_q), .En(InstrEx), .RT(RT), .RTW(RTW), .RA(RA), .AluOp(control_1_aluop),
    .AluD(control_1_alud), .Imm(control_1_imm), .LoD(control_1_lod), .HiD(control_1_hid),
    .Jmp(control_1_jmp), .JT(control_1_jt), .Halt(control_1_halt), .JReg(Halt));  // open: RReg, MemD, RTD, WMem
  alu alu_1 (
    .Op(control_1_aluop), .TData({registerfile_1_da_2, registerfile_1_da}), .AData(registerfile_1_db),
    .RData(alu_1_rdata), .Fl(alu_1_fl));
  assign driver_1_out = control_1_alud ? alu_1_rdata : 16'bz;  // Driver driver_1
  Add #(.Bits(16)) add_1 (.a(PC_out), .b(bitextender_1_out), .c_i(in_6), .s(add_1_s));  // open: c_o
  BitExtender bitextender_1 (.in(control_1_imm), .out(bitextender_1_out));
  // Probe on control_1_imm
  assign driver_1_out = control_1_lod ? {registerfile_1_da_2, control_1_imm} : 16'bz;  // Driver driver_2
  assign driver_1_out = control_1_halt ? add_1_s : 16'bz;  // Driver driver_3
  assign driver_1_out = control_1_hid ? {control_1_imm, registerfile_1_da} : 16'bz;  // Driver driver_4
  // Probe on driver_1_out
  Register #(.Bits(4)) Flags (.D(alu_1_fl), .C(Clk_t), .en(control_1_alud), .Q(Flags_q));
  jumpDecider jumpdecider_1 (.JT(control_1_jt), .Fl(Flags_q), .Jmp(jumpdecider_1_jmp));
  LED led_1 (.in(Flags_q[0]));
  LED led_2 (.in(Flags_q[1]));
  LED led_3 (.in(Flags_q[2]));
  LED led_4 (.in(Flags_q[3]));
  and and_2 (and_2_out, control_1_jmp, jumpdecider_1_jmp);

  // Notes on the sheet:
  //   Imm
  //   Data
  //   fN
  //   fZ
  //   fC
  //   fO
endmodule
